# Fritzing sketch FTDI supporting Arduino v2 (saved by Fritzing 0.9.2b)
circuit board: 8.46099cm x 5.78066cm
breadboards: 1

parts:
  U1 = atmega328 [package=dip]
  FTDI1 = FTDI Friend  # not connected
  C3 = Ceramic Capacitor [capacitance=100nF package="100 mil [THT, multilayer]"]
  FTDI_port = male pin header, 6 pins [form="♂ (male)"]
  Part1 = DeadOn RTC - DS3234 Breakout  # not connected
  RTC_module = female pin header, 6 pins [form="♀ (female)"]
  R2 = Resistor [tolerance=±5% resistance=10k package=THT]
  R3 = Resistor [tolerance=±5% resistance=10k package=THT]
  SDCARD = female pin header, 6 pins [form="♀ (female)"]
  OneWire = female pin header, 3 pins [form="♀ (female)"]
  Reset = Pushbutton [package="[THT]"]
  Wakeup = Pushbutton [package="[THT]"]
  Status = LED - 5mm [color="Red (633nm)" package="5 mm [THT]"]
  Serial_ON/OFF = Pushbutton [package="[THT]"]
  Q1 = NPN-Transistor [package="TO92 [THT]"]
  D1 = Rectifier Diode [part_number=1N4001 package="300 mil [THT]"]
  Analog_sensor = female pin header, 4 pins [form="♀ (female)"]
  D2 = Rectifier Diode [part_number=1N4001 package="300 mil [THT]"]
  VCC1 = Battery
  REG1 = LD33 Low-Dropout Voltage Regulator
  C4 = Electrolytic Capacitor [capacitance=0.33µF package="100 mil [THT, electrolytic]"]
  C5 = Electrolytic Capacitor [capacitance=100nF package="100 mil [THT, electrolytic]"]
  R1 = Resistor [tolerance=±5% resistance=1M package=THT]
  R5 = Resistor [tolerance=±5% resistance=220 package=THT]
  R4 = Resistor [tolerance=±5% resistance=4.7k package=THT]

nets:
  N1: U1.RESET, C3.1, Reset.Pin_1, Reset.Pin_2, R1.Pin_1
  N2: U1.D0_(RX), FTDI_port.pin3
  N3: U1.D1_(TX), FTDI_port.pin2
  N4: U1.D2, RTC_module.pin2, Wakeup.Pin_3, Wakeup.Pin_4
  N5: U1.D3_(PWM), Serial_ON/OFF.Pin_1, Serial_ON/OFF.Pin_2
  N6: U1.D4, Status.anode
  5V/VCC Main: U1.VCC, U1.AVCC, RTC_module.pin5, SDCARD.pin2, Q1.E, Analog_sensor.pin2, REG1.Vout, C4.+
  GND: U1.GND, FTDI_port.pin5, FTDI_port.pin6, RTC_module.pin6, SDCARD.pin1, OneWire.pin1, Reset.Pin_3, Reset.Pin_4, Wakeup.Pin_1, Wakeup.Pin_2, Serial_ON/OFF.Pin_3, Serial_ON/OFF.Pin_4, Analog_sensor.pin1, VCC1.-, REG1.GND, C4.-, C5.-, R1.Pin_0, R5.Pin_0
  N7: U1.D5_(PWM), Q1.B
  N8: U1.D8, OneWire.pin2, R4.Pin_0
  N9: U1.D10_(PWM), SDCARD.pin6
  N10: U1.D11_(PWM), SDCARD.pin4
  N11: U1.D12, SDCARD.pin3
  N12: U1.D13, SDCARD.pin5
  N13: U1.A3, Analog_sensor.pin4
  N14: U1.A4, RTC_module.pin4, R2.Pin_0
  N15: U1.A5, RTC_module.pin3, R3.Pin_1
  N16: C3.0, FTDI_port.pin1
  VCC Supply: FTDI_port.pin4, VCC1.+, REG1.Vin, C5.+
  N17: R2.Pin_1, R3.Pin_0, D1.cathode
  N18: OneWire.pin3, Q1.C, D1.anode, D2.anode, R4.Pin_1
  N19: Status.cathode, R5.Pin_1
  N20: Analog_sensor.pin3, D2.cathode

notes:
  black/GND
  GND
  Project Baseline Oslo
  UW datalogger
  https://github.com/flyhard/UW_datalogger
  VCC
  VCC D5
  A3
  D8
  D12
  D11
  D13
  D10
  A4
  A5
  D2

// code stored in the sketch: Blink.ino
/*
  Blink
  Turns on an LED on for one second, then off for one second, repeatedly.

  Most Arduinos have an on-board LED you can control. On the Uno and
  Leonardo, it is attached to digital pin 13. If you're unsure what
  pin the on-board LED is connected to on your Arduino model, check
  the documentation at http://www.arduino.cc

  This example code is in the public domain.

  modified 8 May 2014
  by Scott Fitzgerald
 */


// the setup function runs once when you press reset or power the board
void setup() {
  // initialize digital pin 13 as an output.
  pinMode(13, OUTPUT);
}

// the loop function runs over and over again forever
void loop() {
  digitalWrite(13, HIGH);   // turn the LED on (HIGH is the voltage level)
  delay(1000);              // wait for a second
  digitalWrite(13, LOW);    // turn the LED off by making the voltage LOW
  delay(1000);              // wait for a second
}

// code stored in the sketch: RTC blink.ino
#include "Wire.h"
#define DS3231_I2C_ADDRESS 0x68
// Convert normal decimal numbers to binary coded decimal
byte decToBcd(byte val)
{
  return( (val/10*16) + (val%10) );
}
// Convert binary coded decimal to normal decimal numbers
byte bcdToDec(byte val)
{
  return( (val/16*10) + (val%16) );
}
void setup()
{
	// initialize digital pin 13 as an output.
  pinMode(13, OUTPUT);
  Wire.begin();
  Serial.begin(9600);
  // set the initial time here:
  // DS3231 seconds, minutes, hours, day, date, month, year
  // setDS3231time(30,42,21,4,26,11,14);
}
void setDS3231time(byte second, byte minute, byte hour, byte dayOfWeek, byte
dayOfMonth, byte month, byte year)
{
  // sets time and date data to DS3231
  Wire.beginTransmission(DS3231_I2C_ADDRESS);
  Wire.write(0); // set next input to start at the seconds register
  Wire.write(decToBcd(second)); // set seconds
  Wire.write(decToBcd(minute)); // set minutes
  Wire.write(decToBcd(hour)); // set hours
  Wire.write(decToBcd(dayOfWeek)); // set day of week (1=Sunday, 7=Saturday)
  Wire.write(decToBcd(dayOfMonth)); // set date (1 to 31)
  Wire.write(decToBcd(month)); // set month
  Wire.write(decToBcd(year)); // set year (0 to 99)
  Wire.endTransmission();
}
void readDS3231time(byte *second,
byte *minute,
byte *hour,
byte *dayOfWeek,
byte *dayOfMonth,
byte *month,
byte *year)
{
  Wire.beginTransmission(DS3231_I2C_ADDRESS);
  Wire.write(0); // set DS3231 register pointer to 00h
  Wire.endTransmission();
  Wire.requestFrom(DS3231_I2C_ADDRESS, 7);
  // request seven bytes of data from DS3231 starting from register 00h
  *second = bcdToDec(Wire.read() & 0x7f);
  *minute = bcdToDec(Wire.read());
  *hour = bcdToDec(Wire.read() & 0x3f);
  *dayOfWeek = bcdToDec(Wire.read());
  *dayOfMonth = bcdToDec(Wire.read());
  *month = bcdToDec(Wire.read());
  *year = bcdToDec(Wire.read());
}
void displayTime()
{
  byte second, minute, hour, dayOfWeek, dayOfMonth, month, year;
  // retrieve data from DS3231
  readDS3231time(&second, &minute, &hour, &dayOfWeek, &dayOfMonth, &month,
  &year);
  // send it to the serial monitor
  Serial.print(hour, DEC);
  // convert the byte variable to a decimal number when displayed
  Serial.print(":");
  if (minute<10)
  {
    Serial.print("0");
  }
  Serial.print(minute, DEC);
  Serial.print(":");
  if (second<10)
  {
    Serial.print("0");
  }
  Serial.print(second, DEC);
  Serial.print(" ");
  Serial.print(dayOfMonth, DEC);
  Serial.print("/");
  Serial.print(month, DEC);
  Serial.print("/");
  Serial.print(year, DEC);
  Serial.print(" Day of week: ");
  switch(dayOfWeek){
  case 1:
    Serial.println("Sunday");
    break;
  case 2:
    Serial.println("Monday");
    break;
  case 3:
    Serial.println("Tuesday");
    break;
  case 4:
    Serial.println("Wednesday");
    break;
  case 5:
    Serial.println("Thursday");
    break;
  case 6:
    Serial.println("Friday");
    break;
  case 7:
    Serial.println("Saturday");
    break;
  }
}
void loop()
{
 	displayTime(); // display the real-time clock data on the Serial Monitor,
	digitalWrite(13, HIGH);   // turn the LED on (HIGH is the voltage level)
  delay(1000);              // wait for a second
	displayTime(); // display the real-time clock data on the Serial Monitor,
  digitalWrite(13, LOW);    // turn the LED off by making the voltage LOW
  delay(1000);              // wait for a second
}
